# Fritzing sketch GS2 (saved by Fritzing 0.9.3b)
breadboards: 1

parts:
  Mod1 = NodeMCU V1.0
  SEN1 = Pulse Sensor [package=SIP]
  M1 = Humidity and Temperature Sensor DHT11

nets:
  VCC: Mod1.3V3, SEN1.Vcc, M1.Vcc
  GND: Mod1.GND, SEN1.GND, M1.GND
  N1: Mod1.TX, M1.Data
  N2: Mod1.A0, SEN1.Signal

custom parts:
  NodeMCU V1.0: ESP8266 based NodeMCU
  Pulse Sensor: Pulse Sensor Optical Heart Rate Monitor for Arduino and other microcontrollers
  Humidity and Temperature Sensor DHT11: Digital relative humidity & temperature sensor DHT11
